// Logisim project cpu8bit.circ as structural Verilog: 10 circuits, main circuit cpu8bit
module cpu8bit (
  input  in_1,
  input  in_2,
  input  in_3,
  input  in_4,
  input  in_5,
  input  in_6,
  input  in_7,
  input  in_8,
  input  in_9,
  input  in_10,
  input  [7:0] RAMoutdata,
  output RAMload,
  output [7:0] RAMindata,
  output [7:0] RAMaddress,
  output out_15,
  output out_16,
  output out_17,
  output out_18,
  output out_19,
  output out_20,
  output out_21,
  output out_22,
  output out_23,
  output out_24,
  output out_25,
  output out_26,
  output out_27,
  output out_28,
  output out_29,
  output out_30
);

  wire decoder_1_aw, decoder_1_imload, decoder_1_inload, decoder_1_irload, decoder_1_pcload, decoder_1_pcsel,
       registers_1_neg, registers_1_zero;
  wire [1:0] decoder_1_addr, decoder_1_aluctrl, decoder_1_areg, decoder_1_breg, decoder_1_dsel;
  wire [7:0] alu_1_r, IM_q, IR_q, multiplexer_1_out, multiplexer_3_out, pc_1_address_2, registers_1_bbus;

  Multiplexer #(.select(2), .width(8), .disabled(0), .enable("false")) multiplexer_1 (
    .in0(IM_q), .in1(RAMoutdata), .in2(alu_1_r), .in3(registers_1_bbus), .out(multiplexer_1_out),
    .sel(decoder_1_dsel));
  PC pc_1 (
    .Address(IM_q), .Address_2(pc_1_address_2), .select(decoder_1_pcsel), .load(decoder_1_pcload),
    .Clock(in_1), .Clr(in_2));
  registers registers_1 (
    .Data(multiplexer_1_out), .Awrite(decoder_1_aw), .Abus(RAMindata), .Bbus(registers_1_bbus),
    .Zero(registers_1_zero), .Neg(registers_1_neg), .Areadreg(decoder_1_areg), .Breadreg(decoder_1_breg),
    .Clock(in_1), .Clear(in_2), .R2({out_23, out_24, out_25, out_26, out_27, out_28, out_29, out_30}),
    .R3({out_15, out_16, out_17, out_18, out_19, out_20, out_21, out_22}));
  Multiplexer #(.select(2), .width(8), .disabled(0), .enable("false")) multiplexer_2 (
    .in0(pc_1_address_2), .in1(IM_q), .in2(registers_1_bbus), .in3(RAMindata), .out(RAMaddress),
    .sel(decoder_1_addr));
  alu alu_1 (.A(RAMindata), .B(registers_1_bbus), .R(alu_1_r), .Ctrl(decoder_1_aluctrl));
  Multiplexer #(.width(8), .disabled(0), .enable("false")) multiplexer_3 (
    .in0(RAMoutdata), .in1({in_3, in_4, in_5, in_6, in_7, in_8, in_9, in_10}), .out(multiplexer_3_out),
    .sel(decoder_1_inload));
  decoder decoder_1 (
    .IR(IR_q), .Clock(in_1), .Clr(in_2), .Zero(registers_1_zero), .Negative(registers_1_neg),
    .Aluctrl(decoder_1_aluctrl), .Areg(decoder_1_areg), .Breg(decoder_1_breg), .IRload(decoder_1_irload),
    .IMload(decoder_1_imload), .PCsel(decoder_1_pcsel), .PCload(decoder_1_pcload), .RAMload(RAMload),
    .Dsel(decoder_1_dsel), .Aw(decoder_1_aw), .Addr(decoder_1_addr), .INload(decoder_1_inload));
  Register IR (.D(RAMoutdata), .en(decoder_1_irload), .Q(IR_q), .clk(in_1), .clr(in_2));
  Register IM (.D(multiplexer_3_out), .en(decoder_1_imload), .Q(IM_q), .clk(in_1), .clr(in_2));

  // Notes on the sheet:
  //   immediate
  //   ram
  //   alu
  //   Bbus
  //   PC
  //   immediate
  //   Bbus
  //   Abus
endmodule

module alu (
  input  [1:0] Ctrl,
  input  [7:0] A,
  input  [7:0] B,
  output [7:0] R
);

  wire n8_bit_adder_1_cout, n8_bit_adder_1_oflw, not_1_out, or_1_out;
  wire [7:0] multiplexer_1_out, n8_bit_adder_1_r, n8_bit_and_1_r, n8_bit_or_1_r;

  _8_bit_AND u_8_bit_and_1 (.A(A), .B(B), .R(n8_bit_and_1_r));
  _8_bit_OR u_8_bit_or_1 (.A(A), .B(B), .R(n8_bit_or_1_r));
  _8_bit_adder u_8_bit_adder_1 (
    .A(A), .B(B), .R(n8_bit_adder_1_r), .Cout(n8_bit_adder_1_cout), .Oflw(n8_bit_adder_1_oflw), .Ctrl(Ctrl[0]));
  Multiplexer #(.width(8), .disabled(0), .enable("false")) multiplexer_1 (
    .in0(n8_bit_and_1_r), .in1(n8_bit_or_1_r), .out(multiplexer_1_out), .sel(Ctrl[0]));
  Multiplexer #(.width(8), .disabled(0), .enable("false")) multiplexer_2 (
    .in0(multiplexer_1_out), .in1(n8_bit_adder_1_r), .out(R), .sel(Ctrl[1]));
  or or_1 (or_1_out, R[0], R[1], R[2], R[3], R[4], R[5], R[6], R[7]);
  not not_1 (not_1_out, or_1_out);
endmodule

module _1_bit_adder (
  input  Cin,
  input  A,
  input  B,
  output Result,
  output Cout
);

  wire and_1_out, and_2_out, xor_1_out;

  and and_1 (and_1_out, B, A);
  xor xor_1 (xor_1_out, A, B);
  and and_2 (and_2_out, xor_1_out, Cin);
  or or_1 (Cout, and_1_out, and_2_out);
  xor xor_2 (Result, Cin, xor_1_out);
endmodule

module _8_bit_adder (
  input  [7:0] A,
  input  Ctrl,
  input  [7:0] B,
  output [7:0] R,
  output Cout,
  output Oflw
);

  wire and_1_out, and_2_out, n1_bit_adder_1_cout, n1_bit_adder_2_cout, n1_bit_adder_3_cout,
       n1_bit_adder_4_cout, n1_bit_adder_5_cout, n1_bit_adder_6_cout, n1_bit_adder_7_cout, not_1_out,
       not_2_out, not_3_out, xor_1_out, xor_2_out, xor_3_out, xor_4_out, xor_5_out, xor_6_out, xor_7_out,
       xor_8_out;

  _1_bit_adder u_1_bit_adder_1 (.A(A[0]), .B(xor_1_out), .Result(R[0]), .Cin(Ctrl), .Cout(n1_bit_adder_1_cout));
  xor xor_1 (xor_1_out, Ctrl, B[0]);
  _1_bit_adder u_1_bit_adder_2 (
    .A(A[1]), .B(xor_2_out), .Result(R[1]), .Cin(n1_bit_adder_1_cout), .Cout(n1_bit_adder_2_cout));
  xor xor_2 (xor_2_out, Ctrl, B[1]);
  _1_bit_adder u_1_bit_adder_3 (
    .A(A[2]), .B(xor_3_out), .Result(R[2]), .Cin(n1_bit_adder_2_cout), .Cout(n1_bit_adder_3_cout));
  xor xor_3 (xor_3_out, Ctrl, B[2]);
  _1_bit_adder u_1_bit_adder_4 (
    .A(A[3]), .B(xor_4_out), .Result(R[3]), .Cin(n1_bit_adder_3_cout), .Cout(n1_bit_adder_4_cout));
  xor xor_4 (xor_4_out, Ctrl, B[3]);
  _1_bit_adder u_1_bit_adder_5 (
    .A(A[4]), .B(xor_5_out), .Result(R[4]), .Cin(n1_bit_adder_4_cout), .Cout(n1_bit_adder_5_cout));
  xor xor_5 (xor_5_out, Ctrl, B[4]);
  _1_bit_adder u_1_bit_adder_6 (
    .A(A[5]), .B(xor_6_out), .Result(R[5]), .Cin(n1_bit_adder_5_cout), .Cout(n1_bit_adder_6_cout));
  xor xor_6 (xor_6_out, Ctrl, B[5]);
  _1_bit_adder u_1_bit_adder_7 (
    .A(A[6]), .B(xor_7_out), .Result(R[6]), .Cin(n1_bit_adder_6_cout), .Cout(n1_bit_adder_7_cout));
  xor xor_7 (xor_7_out, Ctrl, B[6]);
  _1_bit_adder u_1_bit_adder_8 (.A(A[7]), .B(xor_8_out), .Result(R[7]), .Cin(n1_bit_adder_7_cout), .Cout(Cout));
  xor xor_8 (xor_8_out, Ctrl, B[7]);
  not not_1 (not_1_out, R[7]);
  not not_2 (not_2_out, xor_8_out);
  not not_3 (not_3_out, A[7]);
  and and_1 (and_1_out, not_1_out, xor_8_out, A[7]);
  and and_2 (and_2_out, R[7], not_2_out, not_3_out);
  or or_1 (Oflw, and_1_out, and_2_out);
endmodule

module _8_bit_AND (
  input  [7:0] A,
  input  [7:0] B,
  output [7:0] R
);

  and and_1 (R[0], A[0], B[0]);
  and and_2 (R[1], A[1], B[1]);
  and and_3 (R[2], A[2], B[2]);
  and and_4 (R[3], A[3], B[3]);
  and and_5 (R[4], A[4], B[4]);
  and and_6 (R[5], A[5], B[5]);
  and and_7 (R[6], A[6], B[6]);
  and and_8 (R[7], A[7], B[7]);
endmodule

module _8_bit_OR (
  input  [7:0] A,
  input  [7:0] B,
  output [7:0] R
);

  or or_1 (R[0], A[0], B[0]);
  or or_2 (R[1], A[1], B[1]);
  or or_3 (R[2], A[2], B[2]);
  or or_4 (R[3], A[3], B[3]);
  or or_5 (R[4], A[4], B[4]);
  or or_6 (R[5], A[5], B[5]);
  or or_7 (R[6], A[6], B[6]);
  or or_8 (R[7], A[7], B[7]);
endmodule

module registers (
  input  [1:0] Areadreg,
  input  [7:0] Data,
  input  [1:0] Breadreg,
  input  Awrite,
  input  Clock,
  input  Clear,
  output [7:0] Abus,
  output [7:0] Bbus,
  output Zero,
  output Neg,
  output [7:0] R2,
  output [7:0] R3
);

  wire demultiplexer_1_out0, demultiplexer_1_out1, demultiplexer_1_out2, demultiplexer_1_out3, or_1_out;
  wire [7:0] register_1_q, register_2_q;

  Demultiplexer #(.select(2), .disabled(0), .enable("false")) demultiplexer_1 (
    .out0(demultiplexer_1_out0), .out1(demultiplexer_1_out1), .out2(demultiplexer_1_out2),
    .out3(demultiplexer_1_out3), .in(Awrite), .sel(Areadreg));
  Register register_1 (.D(Data), .en(demultiplexer_1_out0), .Q(register_1_q), .clk(Clock), .clr(Clear));
  Register register_2 (.D(Data), .en(demultiplexer_1_out1), .Q(register_2_q), .clk(Clock), .clr(Clear));
  Register register_3 (.D(Data), .en(demultiplexer_1_out2), .Q(R2), .clk(Clock), .clr(Clear));
  Register register_4 (.D(Data), .en(demultiplexer_1_out3), .Q(R3), .clk(Clock), .clr(Clear));
  Multiplexer #(.select(2), .width(8), .disabled(0), .enable("false")) multiplexer_1 (
    .in0(register_1_q), .in1(register_2_q), .in2(R2), .in3(R3), .out(Abus), .sel(Areadreg));
  Multiplexer #(.select(2), .width(8), .disabled(0), .enable("false")) multiplexer_2 (
    .in0(register_1_q), .in1(register_2_q), .in2(R2), .in3(R3), .out(Bbus), .sel(Breadreg));
  or or_1 (or_1_out, Abus[0], Abus[1], Abus[2], Abus[3], Abus[4], Abus[5], Abus[6], Abus[7]);
  not not_1 (Zero, or_1_out);

  assign Neg = Abus[7];
endmodule

module PC (
  input  select,
  input  load,
  input  [7:0] Address,
  input  Clock,
  input  Clr,
  output [7:0] Address_2
);

  wire [7:0] multiplexer_1_out, n8_bit_adder_1_r;

  Multiplexer #(.width(8), .disabled(0), .enable("false")) multiplexer_1 (
    .in0(Address), .in1(n8_bit_adder_1_r), .out(multiplexer_1_out), .sel(select));
  Register register_1 (.D(multiplexer_1_out), .en(load), .Q(Address_2), .clk(Clock), .clr(Clr));
  _8_bit_adder u_8_bit_adder_1 (.A(Address_2), .B(8'h1), .R(n8_bit_adder_1_r), .Ctrl(1'b0));  // open: Cout, Oflw
endmodule

module decoder (
  input  [7:0] IR,
  input  Clock,
  input  Clr,
  input  Zero,
  input  Negative,
  output [1:0] Aluctrl,
  output [1:0] Areg,
  output [1:0] Breg,
  output IRload,
  output INload,
  output IMload,
  output PCsel,
  output PCload,
  output RAMload,
  output [1:0] Dsel,
  output Aw,
  output [1:0] Addr
);

  wire and_1_out, and_2_out, and_3_out, and_4_out, and_5_out, and_6_out, multiplexer_2_out,
       multiplexer_5_out, not_1_out, not_2_out, not_3_out, not_4_out, not_5_out, or_1_out, or_2_out, or_3_out;
  wire [1:0] counter_1_q, multiplexer_1_out, multiplexer_3_out;

  Counter #(.width(2), .max('h3)) counter_1 (
    .Q(counter_1_q), .clk(Clock), .clr(or_1_out));  // open: load, D, count, carry
  or or_1 (or_1_out, Clr, and_1_out);
  and and_1 (and_1_out, counter_1_q[1], counter_1_q[0]);
  not not_1 (not_1_out, IR[7]);
  not not_2 (not_2_out, Zero);
  and and_2 (and_2_out, not_2_out, not_3_out);
  not not_3 (not_3_out, Negative);
  Multiplexer #(.select(4), .width(2), .disabled(0), .enable("false")) multiplexer_1 (
    .in0(2'b10), .in1(2'b10), .in2(2'b10), .in3(2'b10), .in4(2'b01), .in5(2'b00), .in6(2'b11), .in7(2'b00),
    .in8(2'b00), .in9(2'b00), .in10(2'b00), .in11(2'b00), .in12(2'b01), .in13(2'b00), .in14(2'b00),
    .in15(2'b00), .out(multiplexer_1_out), .sel(IR[7:4]));
  Multiplexer #(.select(4), .disabled(0), .enable("false")) multiplexer_2 (
    .in0(1'b1), .in1(1'b1), .in2(1'b1), .in3(1'b1), .in4(1'b1), .in5(1'b0), .in6(1'b1), .in7(1'b1),
    .in8(1'b0), .in9(1'b0), .in10(1'b0), .in11(1'b0), .in12(1'b1), .in13(1'b0), .in14(1'b1), .in15(1'b0),
    .out(multiplexer_2_out), .sel(IR[7:4]));
  Multiplexer #(.select(4), .width(2), .disabled(0), .enable("false")) multiplexer_3 (
    .in0(2'b00), .in1(2'b00), .in2(2'b00), .in3(2'b00), .in4(2'b10), .in5(2'b10), .in6(2'b00), .in7(2'b00),
    .in8(2'b00), .in9(2'b00), .in10(2'b00), .in11(2'b00), .in12(2'b00), .in13(2'b01), .in14(2'b01),
    .in15(2'b00), .out(multiplexer_3_out), .sel(IR[7:4]));
  Multiplexer #(.select(2), .disabled(0), .enable("false")) multiplexer_4 (
    .in0(1'b1), .in1(1'b0), .in2(1'b0), .in3(1'b0), .out(IRload), .sel(counter_1_q));
  and and_3 (and_3_out, IR[4], IR[5], IR[6], not_1_out);
  Multiplexer #(.select(2), .disabled(0), .enable("false")) multiplexer_5 (
    .in0(Zero), .in1(not_2_out), .in2(and_2_out), .in3(Negative), .out(multiplexer_5_out), .sel(IR[5:4]));
  not not_4 (not_4_out, IR[6]);
  not not_5 (not_5_out, IR[5]);
  Multiplexer #(.select(2), .disabled(0), .enable("false")) multiplexer_6 (
    .in0(1'b0), .in1(and_3_out), .in2(1'b0), .in3(1'b0), .out(INload), .sel(counter_1_q));
  or or_2 (or_2_out, and_3_out, IR[7]);
  and and_4 (and_4_out, not_4_out, IR[7], multiplexer_5_out);
  or or_3 (or_3_out, and_4_out, and_5_out);
  and and_5 (and_5_out, IR[4], IR[5], IR[6], IR[7]);
  and and_6 (and_6_out, IR[4], not_5_out, IR[6]);
  Multiplexer #(.select(2), .disabled(0), .enable("false")) multiplexer_7 (
    .in0(1'b0), .in1(or_2_out), .in2(1'b0), .in3(1'b0), .out(IMload), .sel(counter_1_q));
  Multiplexer #(.select(2), .disabled(0), .enable("false")) multiplexer_8 (
    .in0(1'b1), .in1(1'b1), .in2(1'b0), .in3(1'b0), .out(PCsel), .sel(counter_1_q));
  Multiplexer #(.select(2), .disabled(0), .enable("false")) multiplexer_9 (
    .in0(1'b1), .in1(IR[7]), .in2(or_3_out), .in3(1'b0), .out(PCload), .sel(counter_1_q));
  Multiplexer #(.select(2), .disabled(0), .enable("false")) multiplexer_10 (
    .in0(1'b0), .in1(1'b0), .in2(and_6_out), .in3(1'b0), .out(RAMload), .sel(counter_1_q));
  Multiplexer #(.select(2), .width(2), .disabled(0), .enable("false")) multiplexer_11 (
    .in0(2'b00), .in1(2'b00), .in2(multiplexer_1_out), .in3(2'b00), .out(Dsel), .sel(counter_1_q));
  Multiplexer #(.select(2), .disabled(0), .enable("false")) multiplexer_12 (
    .in0(1'b0), .in1(1'b0), .in2(multiplexer_2_out), .in3(1'b0), .out(Aw), .sel(counter_1_q));
  Multiplexer #(.select(2), .width(2), .disabled(0), .enable("false")) multiplexer_13 (
    .in0(2'b00), .in1(2'b00), .in2(multiplexer_3_out), .in3(2'b00), .out(Addr), .sel(counter_1_q));

  assign Aluctrl = IR[5:4];
  assign Areg = IR[3:2];
  assign Breg = IR[1:0];

  // Notes on the sheet:
  //   IR load
  //   IN load
  //   IM load
  //   PC sel
  //   PC load
  //   RAM load
  //   Dsel
  //   Aw
endmodule

module main (
  input  [7:0] in_1,
  output [7:0] out_2
);

  wire button_1_out, button_2_out, clock_1_out, cpu8bit_1_ramload;
  wire [7:0] cpu8bit_1_out_30, cpu8bit_1_ramaddress, cpu8bit_1_ramindata, ram_1_data;

  cpu8bit cpu8bit_1 (
    .in_1(clock_1_out), .in_2(button_1_out), .out_15(out_2[7]), .out_16(out_2[6]), .out_17(out_2[5]),
    .out_18(out_2[4]), .out_19(out_2[3]), .out_20(out_2[2]), .out_21(out_2[1]), .out_22(out_2[0]),
    .in_3(in_1[7]), .in_4(in_1[6]), .in_5(in_1[5]), .in_6(in_1[4]), .in_7(in_1[3]), .in_8(in_1[2]),
    .in_9(in_1[1]), .in_10(in_1[0]), .out_23(cpu8bit_1_out_30[7]), .out_24(cpu8bit_1_out_30[6]),
    .out_25(cpu8bit_1_out_30[5]), .out_26(cpu8bit_1_out_30[4]), .out_27(cpu8bit_1_out_30[3]),
    .out_28(cpu8bit_1_out_30[2]), .out_29(cpu8bit_1_out_30[1]), .out_30(cpu8bit_1_out_30[0]),
    .RAMindata(cpu8bit_1_ramindata), .RAMaddress(cpu8bit_1_ramaddress), .RAMoutdata(ram_1_data),
    .RAMload(cpu8bit_1_ramload));
  Button button_1 (.out(button_1_out));
  Clock clock_1 (.out(clock_1_out));
  RAM #(.bus("separate")) ram_1 (
    .addr(cpu8bit_1_ramaddress), .din(cpu8bit_1_ramindata), .data(ram_1_data), .str(cpu8bit_1_ramload),
    .clk(clock_1_out), .clr(button_2_out));  // open: sel, ld
  Button button_2 (.out(button_2_out));
endmodule
